# Fritzing sketch FingerPrint_Scanner_ESP8266 (saved by Fritzing 0.9.3b)

parts:
  Part1 = Adafruit Feather HUZZAH ESP8266 [part_number="Adafruit #2821"]
  Part2 = Logic Level Converter
  JP1 = Grove Header 4pin Straight direct mount [package=straight]

nets:
  GND: Part1.GND, Part2.GND, JP1.4
  N1: Part1.3.3V, Part2.LV
  N2: Part1.GPIO14/SCK, Part2.TX_LV
  N3: Part1.GPIO12/MISO, Part2.RX_LV
  N4: Part2.TX_HV, JP1.1
  N5: Part2.RX_HV, JP1.2
  N6: Part2.HV, JP1.3

notes:
  (Scanner Module's Interface Port)
  TXD, RXD, VDD, GND
  VDD = +5V (Ext Supply)
  GPIO 12 TXD
  GPIO 14 RXD
  RED LED (Built-in LED)
  Blue LED GPIO 2

custom parts:
  Adafruit Feather HUZZAH ESP8266: his is the Adafruit Feather HUZZAH ESP8266 - our take on an 'all-in-one' ESP8266 WiFi development board with built in USB and battery charging. Its an ESP8266 WiFi module with all the extras you need, ready to rock! We have other boards in the Feather family, check'em out here. At the Feather HUZZAH's heart is an ESP8266 WiFi microcontroller clocked at 80 MHz and at 3.3V logic. This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
  Grove Header 4pin Straight direct mount: Header
